# Fritzing sketch wro tochnopritochno.png (saved by Fritzing 0.9.3b)

parts:
  Raspberry_Pi_1 = Raspberry Pi 3 [part_number=RPI-3-V1.2]
  IC1 = L293D [package=THT]
  S1 = Round Pushbutton
  R1 = Resistor [tolerance=±5% resistance=220 package=THT]
  M1 = DC Motor
  M2 = DC Motor
  VCC2 = 4 x AAA Battery Mount
  hc-sr1 = hc-sr04
  R6 = Resistor [tolerance=±5% resistance=220 package="0402 [SMD]"]
  R7 = Resistor [tolerance=±5% resistance=220 package="0402 [SMD]"]
  R8 = Resistor [tolerance=±5% resistance=220 package="0402 [SMD]"]

nets (from the schematic view):
  GND: Raspberry_Pi_1.GND, Raspberry_Pi_1.GPIO22, IC1.0V, IC1.In_4, R1.Pin_0, hc-sr1.GND
  N1: Raspberry_Pi_1.GPIO17, IC1.Enable_2
  N2: Raspberry_Pi_1.GPIO27, IC1.In_3
  5V: Raspberry_Pi_1.GPIO21, Raspberry_Pi_1.5V, IC1.+V, S1.leg0, R1.Pin_1, hc-sr1.VCC, R7.Pin_0
  N3: Raspberry_Pi_1.GPIO12, R6.Pin_0, R8.Pin_0
  N4: Raspberry_Pi_1.GPIO25, IC1.Enable_1
  N5: Raspberry_Pi_1.GPIO24, IC1.In_1
  N6: Raspberry_Pi_1.GPIO23, IC1.In_2
  N7: IC1.Out_1_(_Controlled_by_Enable_1_), M2.pin_1
  N8: IC1.Out_2_(_Controlled_by_Enable_1_), M2.pin_2
  N9: IC1.+Vmotor, VCC2.+
  N10: IC1.Out_3_(_Controlled_by_Enable_2_), M1.pin_2
  N11: IC1.Out_4_(_Controlled_by_Enable_2_), M1.pin_1
  N12: hc-sr1.Echo, R8.Pin_1
  N13: R6.Pin_1, R7.Pin_1
